# Fritzing sketch Robotika_taviranyitosauto (saved by Fritzing 0.9.9b)
breadboards: 2

parts:
  btnFenyszoro = Pushbutton [package="[THT]"]
  R1 = Rotary Potentiometer (Small) [maximum_resistance=100kΩ package=THT]
  R2 = Rotary Potentiometer (Small) [maximum_resistance=100kΩ package=THT]
  Taviranyito_Arduino = Arduino Uno (Rev3) - ICSP
  R3 = Resistor [tolerance=±5% power=0.25 resistance=10000 package=THT]
  Part2 = Arduino Uno (Rev3) - ICSP
  IC1 = L293D [package=THT]
  M1 = DC Motor
  LED1 = LED - 5mm [color="Yellow (595nm)" current=0.030 package="5 mm [THT]"]
  LED2 = LED - 5mm [color="Yellow (595nm)" current=0.030 package="5 mm [THT]"]
  LED4 = LED - 5mm [color="White (4500K)" current=0.030 package="5 mm [THT]"]
  SP1 = SPEAKER [package=pcb_mount_speaker]
  HC-SR04_Sensor_1 = HC-SR04 Ultrasonic Distance Sensor
  M2 = DC Motor
  VCC1 = Battery block 9V
  R4 = Resistor [tolerance=±5% resistance=220 package="0805 [SMD]"]
  R5 = Resistor [tolerance=±5% resistance=220 package="0805 [SMD]"]

nets:
  N1: btnFenyszoro.Pin_1, btnFenyszoro.Pin_2, R1.leg1, R2.leg1, Taviranyito_Arduino.GND, Taviranyito_Arduino.D1/TX, R3.Pin_0, R3.Pin_1
  N2: btnFenyszoro.Pin_3, btnFenyszoro.Pin_4, R1.leg2, R2.leg2, Taviranyito_Arduino.5V
  N3: R1.wiper, Taviranyito_Arduino.A0
  N4: R2.wiper, Taviranyito_Arduino.A1
  N5: Part2.ICSP_MISO, Part2.D12/MISO, HC-SR04_Sensor_1.ECHO
  N6: Part2.D8, IC1.In_1
  N7: Part2.D9_PWM, IC1.Enable_1
  N8: Part2.D10_PWM/SS, LED1.cathode
  N9: Part2.D11_PWM/MOSI, LED2.cathode
  N10: Part2.D13/SCK, HC-SR04_Sensor_1.TRIG
  GND: Part2.GND, IC1.0V, SP1.+, HC-SR04_Sensor_1.GND, VCC1.-, R4.Pin_1, R5.Pin_1
  N11: Part2.D3_PWM, IC1.Enable_2
  N12: Part2.D4, IC1.In_4
  N13: Part2.D5_PWM, SP1.-
  N14: Part2.D6_PWM, IC1.In_3
  N15: Part2.D7, IC1.In_2
  5V: Part2.5V, IC1.+V, HC-SR04_Sensor_1.VCC
  N16: IC1.Out_1_(_Controlled_by_Enable_1_), M2.pin_2
  N17: IC1.Out_2_(_Controlled_by_Enable_1_), M2.pin_1
  N18: IC1.+Vmotor, VCC1.+
  N19: IC1.Out_3_(_Controlled_by_Enable_2_), M1.pin_2
  N20: IC1.Out_4_(_Controlled_by_Enable_2_), M1.pin_1
  N21: LED1.anode, R5.Pin_0
  N22: LED2.anode, R4.Pin_0
  N23: LED4.cathode, LED4.anode
